// Logisim project psMCU.circ as structural Verilog: 34 circuits, main circuit main
module main (
);

  wire Clk_EN_Toggle_out, Interrupt_out, Manual_Clk_out, NextInst_out, Reset_out, SingleInst_Toggle_out,
       systemsupport_1_led_clk, systemsupport_1_led_clk_en, systemsupport_1_led_clk_ram,
       systemsupport_1_led_singleinst_en;
  wire [9:0] systemsupport_1_userctrl;

  Button SingleInst_Toggle (.out(SingleInst_Toggle_out));
  Button NextInst (.out(NextInst_out));
  Button Clk_EN_Toggle (.out(Clk_EN_Toggle_out));
  Button Manual_Clk (.out(Manual_Clk_out));
  Button Interrupt (.out(Interrupt_out));
  Button Reset (.out(Reset_out));
  psMCU psmcu_1 (.UserCtrl(systemsupport_1_userctrl));
  SystemSupport systemsupport_1 (
    .BTN_SingleInst_Toggle(SingleInst_Toggle_out), .BTN_NextInst(NextInst_out),
    .BTN_ClkEn_Toggle(Clk_EN_Toggle_out), .BTN_ManualClk(Manual_Clk_out), .BTN_Interrupt(Interrupt_out),
    .BTN_Reset(Reset_out), .LED_SingleInst_EN(systemsupport_1_led_singleinst_en),
    .LED_Clk_EN(systemsupport_1_led_clk_en), .LED_Clk_RAM(systemsupport_1_led_clk_ram),
    .LED_Clk(systemsupport_1_led_clk), .UserCtrl(systemsupport_1_userctrl));
  LED SingleInst (.in(systemsupport_1_led_singleinst_en));
  LED CLK_Running (.in(systemsupport_1_led_clk_en));
  LED CLK_RAM (.in(systemsupport_1_led_clk_ram));
  LED CLK (.in(systemsupport_1_led_clk));
endmodule

module Control (
  input  [15:0] Instruction,
  input  Bkpt_Active,
  input  Int_En,
  input  [9:0] UserCtrl,
  output [63:0] Ctrl,
  output Set_Btn_Int_Flag,
  output Int_Active
);

  wire halting_1_halt, interrupt_1_int_ovr, microcoderom_1_out0, microcoderom_1_out1, microcoderom_1_out2,
       microcoderom_1_out3, microcoderom_1_out4, microcoderom_1_out5, microcoderom_1_out6,
       microcoderom_1_out7, microcoderom_2_out0, microcoderom_2_out1, microcoderom_2_out2,
       microcoderom_2_out3, microcoderom_2_out4, microcoderom_2_out5, microcoderom_2_out6,
       microcoderom_2_out7, microcoderom_3_out0, microcoderom_3_out1, microcoderom_3_out2,
       microcoderom_3_out3, microcoderom_3_out4, microcoderom_3_out5, microcoderom_3_out6,
       microcoderom_3_out7, microcoderom_4_out0, microcoderom_4_out1, microcoderom_4_out2,
       microcoderom_4_out3, microcoderom_4_out4, microcoderom_4_out5, microcoderom_4_out6,
       microcoderom_4_out7;
  wire [2:0] subinststepcntr_1_subinststep;
  wire [6:0] decode_1_instcode;

  RisingEdge risingedge_1 (.Q(Set_Btn_Int_Flag), .Inp(UserCtrl[5]), .Clk(UserCtrl[0]));
  Interrupt interrupt_1 (
    .Int_Assert(Set_Btn_Int_Flag), .Int_En(Int_En), .Ctrl(Ctrl), .Int_Ovr(interrupt_1_int_ovr),
    .Int_Active(Int_Active));
  Decode decode_1 (.Instruction(Instruction), .Int_Ovr(interrupt_1_int_ovr), .InstCode(decode_1_instcode));
  SubInstStepCntr subinststepcntr_1 (.Ctrl(Ctrl), .SubInstStep(subinststepcntr_1_subinststep));
  Halting halting_1 (
    .SubInst_Step(subinststepcntr_1_subinststep), .Bkpt_Active(Bkpt_Active), .NextInst(UserCtrl[4]),
    .SingleInst_EN(UserCtrl[6]), .Ctrl(Ctrl), .Halt(halting_1_halt));
  MicroCodeROM microcoderom_1 (
    .SubInstStep(subinststepcntr_1_subinststep), .InstCode(decode_1_instcode), .Halt(halting_1_halt),
    .Out0(microcoderom_1_out0), .Out1(microcoderom_1_out1), .Out2(microcoderom_1_out2),
    .Out3(microcoderom_1_out3), .Out4(microcoderom_1_out4), .Out5(microcoderom_1_out5),
    .Out6(microcoderom_1_out6), .Out7(microcoderom_1_out7));
  MicroCodeROM microcoderom_2 (
    .SubInstStep(subinststepcntr_1_subinststep), .InstCode(decode_1_instcode), .Halt(halting_1_halt),
    .Out0(microcoderom_2_out0), .Out1(microcoderom_2_out1), .Out2(microcoderom_2_out2),
    .Out3(microcoderom_2_out3), .Out4(microcoderom_2_out4), .Out5(microcoderom_2_out5),
    .Out6(microcoderom_2_out6), .Out7(microcoderom_2_out7));
  MicroCodeROM microcoderom_3 (
    .SubInstStep(subinststepcntr_1_subinststep), .InstCode(decode_1_instcode), .Halt(halting_1_halt),
    .Out0(microcoderom_3_out0), .Out1(microcoderom_3_out1), .Out2(microcoderom_3_out2),
    .Out3(microcoderom_3_out3), .Out4(microcoderom_3_out4), .Out5(microcoderom_3_out5),
    .Out6(microcoderom_3_out6), .Out7(microcoderom_3_out7));
  MicroCodeROM microcoderom_4 (
    .SubInstStep(subinststepcntr_1_subinststep), .InstCode(decode_1_instcode), .Halt(halting_1_halt),
    .Out0(microcoderom_4_out0), .Out1(microcoderom_4_out1), .Out2(microcoderom_4_out2),
    .Out3(microcoderom_4_out3), .Out4(microcoderom_4_out4), .Out5(microcoderom_4_out5),
    .Out6(microcoderom_4_out6), .Out7(microcoderom_4_out7));

  // Other names for the same wires on the sheet: CLK = UserCtrl[0]; CLK_RAM = UserCtrl[1]; Reset = UserCtrl[2];
  //   nReset = UserCtrl[3]; NextInst = UserCtrl[4]; BTN_Interrupt = UserCtrl[5]; SingleInst_EN = UserCtrl[6]
endmodule

module SystemSupport (
  input  BTN_SingleInst_Toggle,
  input  BTN_NextInst,
  input  BTN_ClkEn_Toggle,
  input  BTN_ManualClk,
  input  BTN_Interrupt,
  input  BTN_Reset,
  output LED_SingleInst_EN,
  output LED_Clk_EN,
  output LED_Clk_RAM,
  output LED_Clk,
  output [9:0] UserCtrl
);

  wire and_1_out, clock_1_out, counter_1_carry, d_ff_1_q, nand_1_out, or_1_out;
  wire [1:0] counter_1_q;

  not not_1 (UserCtrl[3], BTN_Reset);
  T_Flip_Flop t_ff_1 (.T(1'b1), .clk(BTN_SingleInst_Toggle), .Q(LED_SingleInst_EN));  // open: Qn, reset, preset
  T_Flip_Flop t_ff_2 (.T(1'b1), .clk(BTN_ClkEn_Toggle), .Qn(LED_Clk_EN));  // open: Q, reset, preset
  Clock clock_1 (.out(clock_1_out));
  D_Flip_Flop d_ff_1 (.D(BTN_ManualClk), .clk(clock_1_out), .Q(d_ff_1_q));  // open: Qn, preset, reset
  or or_1 (or_1_out, LED_Clk_EN, and_1_out);
  and and_1 (and_1_out, BTN_ManualClk, ~d_ff_1_q);  // AND_Gate
  nand nand_1 (nand_1_out, ~or_1_out, counter_1_carry);  // NAND_Gate
  Counter #(.max('h3), .width(2)) counter_1 (
    .count(nand_1_out), .Q(counter_1_q), .carry(counter_1_carry), .clk(clock_1_out));  // open: load, D, up, clr
  not not_2 (LED_Clk_RAM, counter_1_q[0]);
  not not_3 (LED_Clk, counter_1_q[1]);

  assign {UserCtrl[6:4], UserCtrl[2:0]} = {LED_SingleInst_EN, BTN_Interrupt, BTN_NextInst, BTN_Reset, LED_Clk_RAM, LED_Clk};

  // Other names for the same wires on the sheet: CLK = LED_Clk; CLK_RAM = LED_Clk_RAM; Reset = BTN_Reset;
  //   nReset = UserCtrl[3]; NextInst = BTN_NextInst; SingleInst_EN = LED_SingleInst_EN
endmodule

module Registers (
  input  [7:0] Mem_Out,
  input  [7:0] Result,
  input  [15:0] Result_Mult,
  input  [63:0] Ctrl,
  output [7:0] RegA,
  output [7:0] RegB
);

  wire A_Latch, B_Latch, CLK, Reset;
  wire [1:0] A_Sel, B_Sel;
  wire [7:0] multiplexer_1_out, multiplexer_2_out;

  Multiplexer #(.select(2), .width(8)) multiplexer_1 (
    .in0(Mem_Out), .in1(Result), .in2(Result_Mult[7:0]), .in3(RegB), .out(multiplexer_1_out), .sel(A_Sel));
  Multiplexer #(.select(2), .width(8)) multiplexer_2 (
    .in0(Mem_Out), .in1(Result), .in2(Result_Mult[7:0]), .in3(RegA), .out(multiplexer_2_out), .sel(B_Sel));
  Register RegisterA (.D(multiplexer_1_out), .en(A_Latch), .clk(CLK), .Q(RegA), .clr(Reset));
  Register RegisterB (.D(multiplexer_2_out), .en(B_Latch), .clk(CLK), .Q(RegB), .clr(Reset));
endmodule

module ProgramCounter (
  input  [15:0] Instruction,
  input  [7:0] Mem_Out,
  input  Conditional,
  input  [63:0] Ctrl,
  output [15:0] PC
);

  wire and_1_out, CLK, Condit_EN, Latch_H, Latch_L, not_1_out, or_1_out, Reset;
  wire [1:0] Sel_Input;
  wire [7:0] multiplexer_4_out, multiplexer_5_out;
  wire [15:0] adder_1_out, bit_extender_1_out, multiplexer_1_out, multiplexer_2_out, multiplexer_3_out;

  and and_1 (and_1_out, Conditional, Condit_EN);
  Multiplexer #(.width(16)) multiplexer_1 (.in0(16'h1), .in1(16'h2), .out(multiplexer_1_out), .sel(and_1_out));
  assign bit_extender_1_out = {{2{Instruction[13]}}, Instruction[13:0]};  // Bit_Extender bit_extender_1
  Multiplexer #(.width(16)) multiplexer_2 (
    .in0(bit_extender_1_out), .in1(multiplexer_1_out), .out(multiplexer_2_out), .sel(not_1_out));
  not not_1 (not_1_out, Sel_Input[0]);
  Adder #(.width(16)) adder_1 (.a(PC), .b(multiplexer_2_out), .out(adder_1_out));  // open: cin, cout
  Multiplexer #(.select(2), .width(16)) multiplexer_3 (
    .in0(adder_1_out), .in1(adder_1_out), .in2(16'h1), .in3({Mem_Out, Mem_Out}), .out(multiplexer_3_out),
    .sel(Sel_Input));
  Multiplexer #(.width(8)) multiplexer_4 (
    .in0(PC[7:0]), .in1(multiplexer_3_out[7:0]), .out(multiplexer_4_out), .sel(Latch_L));
  Multiplexer #(.width(8)) multiplexer_5 (
    .in0(PC[15:8]), .in1(multiplexer_3_out[15:8]), .out(multiplexer_5_out), .sel(Latch_H));
  or or_1 (or_1_out, Latch_L, Latch_H);
  Register #(.width(16)) RegisterPC (
    .D({multiplexer_5_out, multiplexer_4_out}), .en(or_1_out), .clk(CLK), .Q(PC), .clr(Reset));

  // Notes on the sheet:
  //   0 = PC Incr.
  //   1 = PC + Inst
  //   2 = Interrupt Adr.
  //   3 = Mem_Out
endmodule

module InstructionRegister (
  input  [15:0] NextInstruction,
  input  [63:0] Ctrl,
  output [15:0] Instruction
);

  wire CLK, Latch, Reset;

  Register #(.width(16)) RegisterInstruction (.D(NextInstruction), .en(Latch), .clk(CLK), .Q(Instruction), .clr(Reset));
endmodule

module ProgramROM (
  input  [15:0] PC,
  output [15:0] ROMOutput
);

  ROM #(.addrWidth(16), .dataWidth(16)) rom_1 (.addr(PC), .data(ROMOutput));
endmodule

module AddressRegister (
  input  [15:0] PC,
  input  [63:0] Ctrl,
  output [15:0] InstrAddress
);

  wire CLK, Latch, Reset;

  Register #(.width(16)) RegisterInstAdr (.D(PC), .en(Latch), .clk(CLK), .Q(InstrAddress), .clr(Reset));
endmodule

module ALU (
  input  Add_C_In,
  input  Comp_C_In,
  input  [7:0] Shift_In,
  input  in_4,
  input  [7:0] RegA,
  input  [7:0] RegB,
  input  [15:0] Instruction,
  input  in_8,
  input  [63:0] Ctrl,
  output [2:0] Add_Flags,
  output Comp_C_Out,
  output [7:0] Shift_Out,
  output out_13,
  output [7:0] Result,
  output [15:0] Result_Mult
);

  wire Do_B_Comp, Sel_Opr_A;
  wire [1:0] Sel_Opr_B;
  wire [2:0] Sel_Outp;
  wire [7:0] aluadder_1_dataoutput, alubarrelshifter_1_dataoutput, alucomplement_1_dataoutput,
       alulogicoperations_1_output_and, alulogicoperations_1_output_not, alulogicoperations_1_output_or,
       alulogicoperations_1_output_xor, multiplexer_1_out, multiplexer_2_out, multiplexer_3_out;

  Multiplexer #(.width(8)) multiplexer_1 (.in0(RegA), .in1(RegB), .out(multiplexer_1_out), .sel(Sel_Opr_A));
  Multiplexer #(.select(2), .width(8)) multiplexer_2 (
    .in0(RegA), .in1(RegB), .in2(Instruction[7:0]), .in3({8{1'b0}}), .out(multiplexer_2_out), .sel(Sel_Opr_B));
  ALUComplement alucomplement_1 (
    .DataInput(multiplexer_2_out), .C_in(Comp_C_In), .Ctrl(Ctrl), .DataOutput(alucomplement_1_dataoutput),
    .C_out(Comp_C_Out));
  Multiplexer #(.width(8)) multiplexer_3 (
    .in0(multiplexer_2_out), .in1(alucomplement_1_dataoutput), .out(multiplexer_3_out), .sel(Do_B_Comp));
  ALUAdder aluadder_1 (
    .Input_A(multiplexer_1_out), .Input_B(multiplexer_3_out), .C_in(Add_C_In), .Ctrl(Ctrl),
    .DataOutput(aluadder_1_dataoutput), .Flags(Add_Flags));
  ALUBarrelShifter alubarrelshifter_1 (
    .Input_A(multiplexer_1_out), .Input_B(multiplexer_2_out), .Shift_In(Shift_In), .Ctrl(Ctrl),
    .DataOutput(alubarrelshifter_1_dataoutput), .Shift_Out(Shift_Out));
  ALULogicOperations alulogicoperations_1 (
    .Input_A(multiplexer_1_out), .Input_B(multiplexer_2_out), .Output_AND(alulogicoperations_1_output_and),
    .Output_OR(alulogicoperations_1_output_or), .Output_XOR(alulogicoperations_1_output_xor),
    .Output_NOT(alulogicoperations_1_output_not));
  ALUMultiplier alumultiplier_1 (.Input_A(RegA), .Input_B(RegB), .DataOutput(Result_Mult));
  Multiplexer #(.select(3), .width(8)) multiplexer_4 (
    .in0(Instruction[7:0]), .in1(aluadder_1_dataoutput), .in2(alucomplement_1_dataoutput),
    .in3(alubarrelshifter_1_dataoutput), .in4(alulogicoperations_1_output_and),
    .in5(alulogicoperations_1_output_or), .in6(alulogicoperations_1_output_xor),
    .in7(alulogicoperations_1_output_not), .out(Result), .sel(Sel_Outp));

  // Other names for the same wires on the sheet: Inst[15:0] = Instruction
endmodule

module Memory (
  input  [15:0] Instruction,
  input  [15:0] ROMOutput,
  input  [15:0] InstrAddress,
  input  [7:0] RegA,
  input  [7:0] RegB,
  input  [7:0] in_6,
  input  [2:0] Add_Flags,
  input  Comp_C_Out,
  input  [4:0] Comparator,
  input  [6:0] Shift_Out,
  input  Set_Btn_Int_Flag,
  input  [63:0] Ctrl,
  output [7:0] Mem_Out,
  output out_14,
  output Int_EN,
  output [6:0] Shift_In,
  output Add_C_In,
  output Comp_C_In
);

  wire internalperiphs_1_d_out_active, Mem_Ofs_EN, not_1_out, not_2_out, Stack_R;
  wire [2:0] Mem_Sel_Inp;
  wire [6:0] internalperiphs_1_ram_page;
  wire [7:0] heapram_1_d_out, internalperiphs_1_d_out, multiplexer_1_out, multiplexer_3_out,
       multiplexer_4_out, periphbus_1_d_out, stackram_1_d_out;
  wire [8:0] adder_1_out, bit_extender_1_out, multiplexer_2_out;

  assign bit_extender_1_out = {{1{1'b0}}, RegB};  // Bit_Extender bit_extender_1
  Multiplexer #(.select(3), .width(8)) multiplexer_1 (
    .in0(Instruction[7:0]), .in1(ROMOutput[7:0]), .in2(ROMOutput[15:8]), .in3(InstrAddress[7:0]),
    .in4(InstrAddress[15:8]), .in5(RegA), .in6(RegB), .in7({8{1'b0}}), .out(multiplexer_1_out),
    .sel(Mem_Sel_Inp));
  Multiplexer #(.width(9)) multiplexer_2 (
    .in0({9{1'b0}}), .in1(bit_extender_1_out), .out(multiplexer_2_out), .sel(Mem_Ofs_EN));
  Adder #(.width(9)) adder_1 (.a(Instruction[8:0]), .b(multiplexer_2_out), .out(adder_1_out));  // open: cin, cout
  StackRAM stackram_1 (.D_In(multiplexer_1_out), .Adr(adder_1_out), .Ctrl(Ctrl), .D_Out(stackram_1_d_out));
  HeapRAM heapram_1 (
    .D_In(multiplexer_1_out), .Adr(adder_1_out), .Page(internalperiphs_1_ram_page), .Ctrl(Ctrl),
    .D_Out(heapram_1_d_out));  // open: in_3, in_5
  InternalPeriphs internalperiphs_1 (
    .D_In(multiplexer_1_out), .Adr(adder_1_out), .Add_Flags(Add_Flags), .Comp_C_Out(Comp_C_Out),
    .Shift_Out(Shift_Out), .ComparatorOut(Comparator), .Set_Btn_Int_Flag(Set_Btn_Int_Flag), .Ctrl(Ctrl),
    .D_Out(internalperiphs_1_d_out), .D_Out_Active(internalperiphs_1_d_out_active),
    .RAM_Page(internalperiphs_1_ram_page), .Int_EN(Int_EN), .Shift_In(Shift_In), .Add_C_In(Add_C_In),
    .Comp_C_In(Comp_C_In));  // open: in_3, out_12
  PeriphBus periphbus_1 (.D_In(multiplexer_1_out), .Adr(adder_1_out), .D_Out(periphbus_1_d_out));
  not not_1 (not_1_out, internalperiphs_1_d_out_active);
  Multiplexer #(.width(8)) multiplexer_3 (
    .in0(heapram_1_d_out), .in1(multiplexer_4_out), .out(multiplexer_3_out), .sel(adder_1_out[8]));
  Multiplexer #(.width(8)) multiplexer_4 (
    .in0(internalperiphs_1_d_out), .in1(periphbus_1_d_out), .out(multiplexer_4_out), .sel(not_1_out));
  not not_2 (not_2_out, Stack_R);
  Multiplexer #(.width(8)) multiplexer_5 (
    .in0(stackram_1_d_out), .in1(multiplexer_3_out), .out(Mem_Out), .sel(not_2_out));

  // Other names for the same wires on the sheet: A[7:0] = RegA; B[7:0] = RegB; Com_C_Out = Comp_C_Out;
  //   IAdr[15:0] = InstrAddress; Inst[15:0] = Instruction; ROM_Out[15:0] = ROMOutput
endmodule

module Conditional (
  input  [7:0] RegA,
  input  [7:0] Mem_Out,
  input  [15:0] Instruction,
  input  [63:0] Ctrl
);

  wire Bit_State, Conditional, multiplexer_2_out, Sel_Input;
  wire [7:0] multiplexer_1_out;

  Multiplexer #(.width(8)) multiplexer_1 (.in0(RegA), .in1(Mem_Out), .out(multiplexer_1_out), .sel(Sel_Input));
  Multiplexer #(.select(3)) multiplexer_2 (
    .in0(multiplexer_1_out[0]), .in1(multiplexer_1_out[1]), .in2(multiplexer_1_out[2]),
    .in3(multiplexer_1_out[3]), .in4(multiplexer_1_out[4]), .in5(multiplexer_1_out[5]),
    .in6(multiplexer_1_out[6]), .in7(multiplexer_1_out[7]), .out(multiplexer_2_out), .sel(Instruction[11:9]));
  xnor xnor_1 (Conditional, multiplexer_2_out, Bit_State);
endmodule

module HeapRAM (
  input  [7:0] D_In,
  input  [8:0] Adr,
  input  in_3,
  input  [6:0] Page,
  input  in_5,
  input  [63:0] Ctrl,
  output [7:0] D_Out
);

  wire CLK_RAM, not_1_out, RAM_R, RAM_W, register_1_q, Reset;

  Register #(.trigger("falling"), .width(1)) register_1 (
    .D(RAM_W), .en(1'b1), .clk(CLK_RAM), .Q(register_1_q), .clr(Reset));
  RAM #(.addrWidth(15), .databus("bidir"), .trigger("high")) ram_1 (
    .addr({Page, Adr[7:0]}), .we(register_1_q), .oe(RAM_R), .data(D_Out));
  assign D_Out = not_1_out ? D_In : 8'bz;  // Controlled_Buffer controlled_buffer_1
  not not_1 (not_1_out, RAM_R);
endmodule

module StackRAM (
  input  [7:0] D_In,
  input  [8:0] Adr,
  input  [63:0] Ctrl,
  output [7:0] D_Out
);

  wire CLK, CLK_RAM, Latch_Ptr, R, register_2_q, Reset, Sel_Adr, W;
  wire [1:0] Sel_Ofs;
  wire [14:0] adder_1_out, bit_extender_1_out, multiplexer_1_out, multiplexer_2_out, register_1_q;

  Register #(.width(15)) register_1 (.D(adder_1_out), .en(Latch_Ptr), .clk(CLK), .Q(register_1_q), .clr(Reset));
  assign bit_extender_1_out = {{6{Sel_Ofs[0]}}, Adr};  // Bit_Extender bit_extender_1
  Multiplexer #(.select(2), .width(15)) multiplexer_1 (
    .in0(15'h1), .in1({15{1'b1}}), .in2(bit_extender_1_out), .in3(bit_extender_1_out),
    .out(multiplexer_1_out), .sel(Sel_Ofs));
  Adder #(.width(15)) adder_1 (.a(register_1_q), .b(multiplexer_1_out), .out(adder_1_out));  // open: cin, cout
  Multiplexer #(.width(15)) multiplexer_2 (
    .in0(register_1_q), .in1(adder_1_out), .out(multiplexer_2_out), .sel(Sel_Adr));
  Register #(.trigger("falling"), .width(1)) register_2 (
    .D(W), .en(1'b1), .clk(CLK_RAM), .Q(register_2_q), .clr(Reset));
  RAM #(.addrWidth(15), .databus("bidir"), .trigger("high")) ram_1 (
    .addr(multiplexer_2_out), .we(register_2_q), .oe(R), .data(D_Out));
  assign D_Out = R ? D_In : 8'bz;  // Controlled_Buffer controlled_buffer_1
endmodule

module InternalPeriphs (
  input  [7:0] D_In,
  input  [8:0] Adr,
  input  in_3,
  input  [2:0] Add_Flags,
  input  Comp_C_Out,
  input  [6:0] Shift_Out,
  input  [4:0] ComparatorOut,
  input  Set_Btn_Int_Flag,
  input  [63:0] Ctrl,
  output [7:0] D_Out,
  output D_Out_Active,
  output out_12,
  output [6:0] RAM_Page,
  output Int_EN,
  output [6:0] Shift_In,
  output Add_C_In,
  output Comp_C_In
);

  wire comparator_1_eq;
  wire [7:0] regsys1_1_d_out, regsys2_1_d_out, regsys3_1_d_out, regsys4_1_d_out;

  Comparator #(.width(7)) comparator_1 (.a(Adr[8:2]), .b(7'b1100000), .eq(comparator_1_eq));  // open: gt, lt
  RegSYS1 regsys1_1 (
    .D_In(D_In), .Add_Flags(Add_Flags), .Comp_C_Out(Comp_C_Out), .Ctrl(Ctrl), .D_Out(regsys1_1_d_out),
    .Add_C_In(Add_C_In), .Comp_C_In(Comp_C_In));  // open: in_4
  RegSYS2 regsys2_1 (.D_In(D_In), .Ctrl(Ctrl), .D_Out(regsys2_1_d_out), .RAM_Page(RAM_Page));
  RegSYS3 regsys3_1 (
    .D_In(D_In), .ComparatorOut(ComparatorOut), .Set_Btn_Int_Flag(Set_Btn_Int_Flag), .Ctrl(Ctrl),
    .D_Out(regsys3_1_d_out), .Int_EN(Int_EN));
  RegSYS4 regsys4_1 (.D_In(D_In), .Shift_Out(Shift_Out), .Ctrl(Ctrl), .D_Out(regsys4_1_d_out), .Shift_In(Shift_In));
  Multiplexer #(.select(2), .width(8)) multiplexer_1 (
    .in0(regsys1_1_d_out), .in1(regsys2_1_d_out), .in2(regsys3_1_d_out), .in3(regsys4_1_d_out), .out(D_Out),
    .sel(Adr[1:0]));
endmodule

module PeriphBus (
  input  [7:0] D_In,
  input  [8:0] Adr,
  output [7:0] D_Out
);
endmodule

module Decode (
  input  [15:0] Instruction,
  input  Int_Ovr,
  output [6:0] InstCode
);

  ROM #(.addrWidth(9), .dataWidth(7)) rom_1 (.addr({Int_Ovr, Instruction[15:8]}), .data(InstCode));
endmodule

module ALUComplement (
  input  [7:0] DataInput,
  input  C_in,
  input  [63:0] Ctrl,
  output [7:0] DataOutput,
  output C_out
);

  wire DoCarry, multiplexer_1_out;
  wire [7:0] not_1_out;

  Multiplexer multiplexer_1 (.in0(1'b1), .in1(C_in), .out(multiplexer_1_out), .sel(DoCarry));
  assign not_1_out = ~DataInput;  // NOT_Gate not_1, 8 bits wide
  Adder adder_1 (.a({8{1'b0}}), .b(not_1_out), .out(DataOutput), .cin(multiplexer_1_out), .cout(C_out));

  // Other names for the same wires on the sheet: Data[7:0] = DataInput
endmodule

module ALUAdder (
  input  [7:0] Input_A,
  input  [7:0] Input_B,
  input  C_in,
  input  [63:0] Ctrl,
  output [7:0] DataOutput,
  output [2:0] Flags
);

  wire and_1_out, and_2_out, and_3_out, DoCarry;

  and and_1 (and_1_out, C_in, DoCarry);
  Adder #(.width(4)) adder_1 (
    .a(Input_A[3:0]), .b(Input_B[3:0]), .out(DataOutput[3:0]), .cin(and_1_out), .cout(Flags[1]));
  Adder #(.width(4)) adder_2 (
    .a(Input_A[7:4]), .b(Input_B[7:4]), .out(DataOutput[7:4]), .cin(Flags[1]), .cout(Flags[0]));
  and and_2 (and_2_out, ~DataOutput[7], Input_A[7], Input_B[7]);  // AND_Gate
  and and_3 (and_3_out, DataOutput[7], ~Input_A[7], ~Input_B[7]);  // AND_Gate
  or or_1 (Flags[2], and_2_out, and_3_out);

  // Other names for the same wires on the sheet: A[7:0] = Input_A; B[7:0] = Input_B
endmodule

module ALULogicOperations (
  input  [7:0] Input_A,
  input  [7:0] Input_B,
  output [7:0] Output_AND,
  output [7:0] Output_OR,
  output [7:0] Output_XOR,
  output [7:0] Output_NOT
);

  assign Output_AND = Input_A & Input_B;  // AND_Gate and_1, 8 bits wide
  assign Output_OR = Input_A | Input_B;  // OR_Gate or_1, 8 bits wide
  assign Output_XOR = Input_A ^ Input_B;  // XOR_Gate xor_1, 8 bits wide
  assign Output_NOT = ~Input_A;  // NOT_Gate not_1, 8 bits wide
endmodule

module ALUBarrelShifter (
  input  [7:0] Input_A,
  input  [7:0] Input_B,
  input  [7:0] Shift_In,
  input  [63:0] Ctrl,
  output [7:0] DataOutput,
  output [7:0] Shift_Out
);

  wire and_1_out, and_2_out, and_3_out, Dir, multiplexer_1_out, multiplexer_2_out, multiplexer_3_out,
       multiplexer_4_out, multiplexer_5_out, multiplexer_6_out, multiplexer_7_out, multiplexer_8_out,
       multiplexer_9_out, multiplexer_10_out, multiplexer_11_out, multiplexer_12_out, multiplexer_13_out,
       multiplexer_14_out, multiplexer_15_out, multiplexer_16_out, multiplexer_17_out, multiplexer_18_out,
       multiplexer_19_out, multiplexer_20_out, multiplexer_21_out, multiplexer_22_out, multiplexer_23_out,
       multiplexer_24_out, multiplexer_25_out, multiplexer_26_out, multiplexer_27_out, multiplexer_28_out,
       multiplexer_29_out, multiplexer_30_out, multiplexer_31_out, multiplexer_32_out, multiplexer_33_out,
       multiplexer_34_out, multiplexer_35_out, multiplexer_36_out, multiplexer_37_out;

  Multiplexer multiplexer_1 (.in0(Input_A[0]), .in1(Input_A[7]), .out(multiplexer_1_out), .sel(Dir));
  Multiplexer multiplexer_2 (.in0(Input_A[1]), .in1(Input_A[6]), .out(multiplexer_2_out), .sel(Dir));
  Multiplexer multiplexer_3 (.in0(Input_A[2]), .in1(Input_A[5]), .out(multiplexer_3_out), .sel(Dir));
  Multiplexer multiplexer_4 (.in0(Input_A[3]), .in1(Input_A[4]), .out(multiplexer_4_out), .sel(Dir));
  Multiplexer multiplexer_5 (.in0(Input_A[4]), .in1(Input_A[3]), .out(multiplexer_5_out), .sel(Dir));
  Multiplexer multiplexer_6 (.in0(Input_A[5]), .in1(Input_A[2]), .out(multiplexer_6_out), .sel(Dir));
  Multiplexer multiplexer_7 (.in0(Input_A[6]), .in1(Input_A[1]), .out(multiplexer_7_out), .sel(Dir));
  Multiplexer multiplexer_8 (.in0(Input_A[7]), .in1(Input_A[0]), .out(multiplexer_8_out), .sel(Dir));
  Multiplexer multiplexer_9 (
    .in0(multiplexer_18_out), .in1(multiplexer_20_out), .out(multiplexer_9_out), .sel(Input_B[1]));
  Multiplexer multiplexer_10 (
    .in0(multiplexer_1_out), .in1(multiplexer_9_out), .out(multiplexer_10_out), .sel(Input_B[0]));
  Multiplexer multiplexer_11 (
    .in0(multiplexer_2_out), .in1(multiplexer_1_out), .out(multiplexer_11_out), .sel(Input_B[0]));
  Multiplexer multiplexer_12 (
    .in0(multiplexer_3_out), .in1(multiplexer_2_out), .out(multiplexer_12_out), .sel(Input_B[0]));
  Multiplexer multiplexer_13 (
    .in0(multiplexer_4_out), .in1(multiplexer_3_out), .out(multiplexer_13_out), .sel(Input_B[0]));
  Multiplexer multiplexer_14 (
    .in0(multiplexer_5_out), .in1(multiplexer_4_out), .out(multiplexer_14_out), .sel(Input_B[0]));
  Multiplexer multiplexer_15 (
    .in0(multiplexer_6_out), .in1(multiplexer_5_out), .out(multiplexer_15_out), .sel(Input_B[0]));
  Multiplexer multiplexer_16 (
    .in0(multiplexer_7_out), .in1(multiplexer_6_out), .out(multiplexer_16_out), .sel(Input_B[0]));
  Multiplexer multiplexer_17 (
    .in0(multiplexer_8_out), .in1(multiplexer_7_out), .out(multiplexer_17_out), .sel(Input_B[0]));
  and and_1 (and_1_out, multiplexer_8_out, Input_B[0]);
  Multiplexer multiplexer_18 (.in0(Shift_In[0]), .in1(Shift_In[4]), .out(multiplexer_18_out), .sel(Input_B[2]));
  Multiplexer multiplexer_19 (.in0(Shift_In[1]), .in1(Shift_In[5]), .out(multiplexer_19_out), .sel(Input_B[2]));
  Multiplexer multiplexer_20 (.in0(Shift_In[2]), .in1(Shift_In[6]), .out(multiplexer_20_out), .sel(Input_B[2]));
  Multiplexer multiplexer_21 (
    .in0(multiplexer_10_out), .in1(multiplexer_18_out), .out(multiplexer_21_out), .sel(Input_B[1]));
  Multiplexer multiplexer_22 (
    .in0(multiplexer_11_out), .in1(multiplexer_19_out), .out(multiplexer_22_out), .sel(Input_B[1]));
  Multiplexer multiplexer_23 (
    .in0(multiplexer_12_out), .in1(multiplexer_10_out), .out(multiplexer_23_out), .sel(Input_B[1]));
  Multiplexer multiplexer_24 (
    .in0(multiplexer_13_out), .in1(multiplexer_11_out), .out(multiplexer_24_out), .sel(Input_B[1]));
  Multiplexer multiplexer_25 (
    .in0(multiplexer_14_out), .in1(multiplexer_12_out), .out(multiplexer_25_out), .sel(Input_B[1]));
  Multiplexer multiplexer_26 (
    .in0(multiplexer_15_out), .in1(multiplexer_13_out), .out(multiplexer_26_out), .sel(Input_B[1]));
  Multiplexer multiplexer_27 (
    .in0(multiplexer_16_out), .in1(multiplexer_14_out), .out(multiplexer_27_out), .sel(Input_B[1]));
  Multiplexer multiplexer_28 (
    .in0(multiplexer_17_out), .in1(multiplexer_15_out), .out(multiplexer_28_out), .sel(Input_B[1]));
  Multiplexer multiplexer_29 (.in0(and_1_out), .in1(multiplexer_16_out), .out(multiplexer_29_out), .sel(Input_B[1]));
  and and_2 (and_2_out, Input_B[1], multiplexer_17_out);
  and and_3 (and_3_out, Input_B[1], and_1_out);
  Multiplexer multiplexer_30 (.in0(multiplexer_21_out), .in1(Shift_In[0]), .out(multiplexer_30_out), .sel(Input_B[2]));
  Multiplexer multiplexer_31 (.in0(multiplexer_22_out), .in1(Shift_In[1]), .out(multiplexer_31_out), .sel(Input_B[2]));
  Multiplexer multiplexer_32 (.in0(multiplexer_23_out), .in1(Shift_In[2]), .out(multiplexer_32_out), .sel(Input_B[2]));
  Multiplexer multiplexer_33 (.in0(multiplexer_24_out), .in1(Shift_In[3]), .out(multiplexer_33_out), .sel(Input_B[2]));
  Multiplexer multiplexer_34 (
    .in0(multiplexer_25_out), .in1(multiplexer_21_out), .out(multiplexer_34_out), .sel(Input_B[2]));
  Multiplexer multiplexer_35 (
    .in0(multiplexer_26_out), .in1(multiplexer_22_out), .out(multiplexer_35_out), .sel(Input_B[2]));
  Multiplexer multiplexer_36 (
    .in0(multiplexer_27_out), .in1(multiplexer_23_out), .out(multiplexer_36_out), .sel(Input_B[2]));
  Multiplexer multiplexer_37 (
    .in0(multiplexer_28_out), .in1(multiplexer_24_out), .out(multiplexer_37_out), .sel(Input_B[2]));
  Multiplexer multiplexer_38 (.in0(multiplexer_29_out), .in1(multiplexer_25_out), .out(Shift_Out[0]), .sel(Input_B[2]));
  Multiplexer multiplexer_39 (.in0(and_2_out), .in1(multiplexer_26_out), .out(Shift_Out[1]), .sel(Input_B[2]));
  Multiplexer multiplexer_40 (.in0(and_3_out), .in1(multiplexer_27_out), .out(Shift_Out[2]), .sel(Input_B[2]));
  and and_4 (Shift_Out[3], multiplexer_28_out, Input_B[2]);
  and and_5 (Shift_Out[4], multiplexer_29_out, Input_B[2]);
  and and_6 (Shift_Out[5], and_2_out, Input_B[2]);
  and and_7 (Shift_Out[6], and_3_out, Input_B[2]);
  Multiplexer multiplexer_41 (.in0(multiplexer_30_out), .in1(multiplexer_37_out), .out(DataOutput[0]), .sel(Dir));
  Multiplexer multiplexer_42 (.in0(multiplexer_31_out), .in1(multiplexer_36_out), .out(DataOutput[1]), .sel(Dir));
  Multiplexer multiplexer_43 (.in0(multiplexer_32_out), .in1(multiplexer_35_out), .out(DataOutput[2]), .sel(Dir));
  Multiplexer multiplexer_44 (.in0(multiplexer_33_out), .in1(multiplexer_34_out), .out(DataOutput[3]), .sel(Dir));
  Multiplexer multiplexer_45 (.in0(multiplexer_34_out), .in1(multiplexer_33_out), .out(DataOutput[4]), .sel(Dir));
  Multiplexer multiplexer_46 (.in0(multiplexer_35_out), .in1(multiplexer_32_out), .out(DataOutput[5]), .sel(Dir));
  Multiplexer multiplexer_47 (.in0(multiplexer_36_out), .in1(multiplexer_31_out), .out(DataOutput[6]), .sel(Dir));
  Multiplexer multiplexer_48 (.in0(multiplexer_37_out), .in1(multiplexer_30_out), .out(DataOutput[7]), .sel(Dir));

  assign Shift_Out[7] = 1'b0;

  // Other names for the same wires on the sheet: A[7:0] = Input_A; B[7:0] = Input_B
endmodule

module ALUMultiplier (
  input  [7:0] Input_A,
  input  [7:0] Input_B,
  output [15:0] DataOutput
);

  Multiplier multiplier_1 (.a(Input_A), .b(Input_B), .out(DataOutput[7:0]), .cout(DataOutput[15:8]));  // open: cin
endmodule

module RegSYS1 (
  input  [7:0] D_In,
  input  [2:0] Add_Flags,
  input  Comp_C_Out,
  input  in_4,
  input  [63:0] Ctrl,
  output [7:0] D_Out,
  output Add_C_In,
  output Comp_C_In
);
endmodule

module RegSYS2 (
  input  [7:0] D_In,
  input  [63:0] Ctrl,
  output [7:0] D_Out,
  output [6:0] RAM_Page
);
endmodule

module RegSYS3 (
  input  [7:0] D_In,
  input  [4:0] ComparatorOut,
  input  Set_Btn_Int_Flag,
  input  [63:0] Ctrl,
  output [7:0] D_Out,
  output Int_EN
);
endmodule

module RegSYS4 (
  input  [7:0] D_In,
  input  [6:0] Shift_Out,
  input  [63:0] Ctrl,
  output [7:0] D_Out,
  output [6:0] Shift_In
);
endmodule

module Interrupt (
  input  Int_Assert,
  input  Int_En,
  input  [63:0] Ctrl,
  output Int_Ovr,
  output Int_Active
);

  wire and_1_out, CLK, Int_Clr, Int_Override_Clr, IReg_Latch, Reset, sr_ff_rprio_1_q;

  SR_FF_Rprio sr_ff_rprio_1 (.Q(sr_ff_rprio_1_q), .S(Int_Assert), .R(and_1_out), .Clk(CLK), .Reset(Reset));
  and and_1 (and_1_out, sr_ff_rprio_1_q, Int_En, IReg_Latch, ~Int_Active);  // AND_Gate
  SR_FF_Rprio sr_ff_rprio_2 (.Q(Int_Ovr), .S(and_1_out), .R(Int_Override_Clr), .Clk(CLK), .Reset(Reset));
  SR_FF_Rprio sr_ff_rprio_3 (.Q(Int_Active), .S(and_1_out), .R(Int_Clr), .Clk(CLK), .Reset(Reset));
endmodule

module Halting (
  input  [2:0] SubInst_Step,
  input  Bkpt_Active,
  input  NextInst,
  input  SingleInst_EN,
  input  [63:0] Ctrl,
  output Halt
);

  wire and_1_out, CLK, comparator_1_eq, Halt_Clr, Halt_Set, or_1_out, or_2_out, Reset, risingedge_1_q,
       sr_ff_rprio_1_q;

  or or_1 (or_1_out, SingleInst_EN, Bkpt_Active);
  Comparator #(.mode("unsigned"), .width(3)) comparator_1 (
    .a(SubInst_Step), .b(3'b000), .eq(comparator_1_eq));  // open: gt, lt
  and and_1 (and_1_out, or_1_out, comparator_1_eq);
  SR_FF_Rprio sr_ff_rprio_1 (.Q(sr_ff_rprio_1_q), .S(Halt_Set), .R(Halt_Clr), .Clk(CLK), .Reset(Reset));
  or or_2 (or_2_out, and_1_out, sr_ff_rprio_1_q);
  RisingEdge risingedge_1 (.Q(risingedge_1_q), .Inp(NextInst), .Clk(CLK));
  and and_2 (Halt, or_2_out, ~risingedge_1_q);  // AND_Gate
endmodule

module SubInstStepCntr (
  input  [63:0] Ctrl,
  output [2:0] SubInstStep
);

  wire CLK, Reset, SubInst_Clr, SubInst_Inc;

  Counter #(.max('h7), .width(3)) counter_1 (
    .clr(Reset), .load(SubInst_Clr), .up(1'b1), .count(SubInst_Inc), .clk(CLK), .D(3'b000), .Q(SubInstStep));  // open: carry
endmodule

module MicroCodeROM (
  input  [2:0] SubInstStep,
  input  [6:0] InstCode,
  input  Halt,
  output Out0,
  output Out1,
  output Out2,
  output Out3,
  output Out4,
  output Out5,
  output Out6,
  output Out7
);

  ROM #(.addrWidth(11)) rom_1 (
    .addr({Halt, InstCode, SubInstStep}), .data({Out7, Out6, Out5, Out4, Out3, Out2, Out1, Out0}));
endmodule

module psMCU (
  input  [9:0] UserCtrl
);

  wire [63:0] Ctrl;

  Conditional conditional_1 (.Ctrl(Ctrl));  // open: RegA, Mem_Out, Instruction
  ProgramCounter programcounter_1 (.Ctrl(Ctrl));  // open: PC, Instruction, Mem_Out, Conditional
  Registers registers_1 (.Ctrl(Ctrl));  // open: RegA, RegB, Mem_Out, Result, Result_Mult
  AddressRegister addressregister_1 (.Ctrl(Ctrl));  // open: InstrAddress, PC
  InstructionRegister instructionregister_1 (.Ctrl(Ctrl));  // open: Instruction, NextInstruction
  ProgramROM programrom_1 ();  // open: PC, ROMOutput
  RegisterComparator registercomparator_1 ();  // open: RegA, RegB, ComparatorOut
  Breakpoint breakpoint_1 ();  // open: InstrAddress, Active
  ALU alu_1 (.Ctrl(Ctrl));  // open: Result_Mult, Result, Add_Flags, Comp_C_Out, Shift_Out, out_13, Add_C_In, Comp_C_In, Shift_In, in_4, RegA, RegB, Instruction, in_8
  Control control_1 (
    .UserCtrl(UserCtrl), .Ctrl(Ctrl));  // open: Instruction, Bkpt_Active, Int_En, Set_Btn_Int_Flag, Int_Active
  Memory memory_1 ();  // open: Instruction, ROMOutput, InstrAddress, RegA, RegB, in_6, Add_Flags, Comp_C_Out, Comparator, Shift_Out, Set_Btn_Int_Flag, Ctrl, Mem_Out, out_14, Int_EN, Shift_In, Add_C_In, Comp_C_In
endmodule

module RegisterComparator (
  input  [7:0] RegA,
  input  [7:0] RegB,
  output [4:0] ComparatorOut
);

  Comparator #(.mode("unsigned")) comparator_1 (
    .a(RegA), .b(RegB), .gt(ComparatorOut[3]), .eq(ComparatorOut[2]), .lt(ComparatorOut[4]));
  Comparator #(.mode("unsigned")) comparator_2 (.a(RegB), .b({8{1'b0}}), .eq(ComparatorOut[1]));  // open: gt, lt
  Comparator #(.mode("unsigned")) comparator_3 (.a(RegA), .b({8{1'b0}}), .eq(ComparatorOut[0]));  // open: gt, lt
endmodule

module Breakpoint (
  input  [15:0] InstrAddress,
  output Active
);

  wire comparator_1_eq;

  Comparator #(.mode("unsigned"), .width(16)) comparator_1 (
    .a(InstrAddress), .b({16{1'b1}}), .eq(comparator_1_eq));  // open: gt, lt
  and and_1 (Active, comparator_1_eq, 1'b0);

  // Notes on the sheet:
  //   Adr:
  //   En:
endmodule

module RisingEdge (
  input  Inp,
  input  Clk,
  output Q
);

  wire d_ff_1_q, d_ff_2_q;

  D_Flip_Flop d_ff_1 (.D(Inp), .clk(Clk), .Q(d_ff_1_q));  // open: Qn, preset, reset
  D_Flip_Flop d_ff_2 (.D(d_ff_1_q), .clk(Clk), .Q(d_ff_2_q));  // open: Qn, preset, reset
  and and_1 (Q, d_ff_1_q, ~d_ff_2_q);  // AND_Gate
endmodule

module SR_FF_Rprio (
  input  S,
  input  R,
  input  Clk,
  input  Reset,
  output Q
);

  wire and_1_out;

  and and_1 (and_1_out, S, ~R);  // AND_Gate
  S_R_Flip_Flop s_r_ff_1 (.S(and_1_out), .R(R), .clk(Clk), .Q(Q), .reset(Reset));  // open: Qn, preset
endmodule
